// Logisim project Adder.circ as structural Verilog: 1 circuit, main circuit main
module main (
  input  [2:0] A,
  input  [2:0] B,
  output out_3
);

  wire [2:0] adder_1_out;

  Adder #(.width(3)) adder_1 (.a(A), .b(3'b100), .out(adder_1_out));  // open: cin, cout
  Comparator #(.width(3)) comparator_1 (.a(adder_1_out), .b(B), .eq(out_3));  // open: gt, lt

  // Notes on the sheet:
  //   Does B equal to A + 4?
endmodule
