// Logisim project Multiplexer.circ as structural Verilog: 1 circuit, main circuit main
module main (
  input  [1:0] in_1,
  output [7:0] out_2
);

  Multiplexer #(.select(2), .width(8), .enable("false")) multiplexer_1 (
    .in0(8'h1), .in1(8'h2), .in2(8'h4), .in3(8'h9), .out(out_2), .sel(in_1));
endmodule
